# Fritzing sketch pcb_volledig (saved by Fritzing 0.9.3b)
circuit board: 8.46667cm x 5.64444cm
breadboards: 1

parts:
  MH-ET_LIVE_ESP32_DEVKIT1 = MH-ET LIVE ESP32 DEVKIT 38 pins
  S1 = H-Bridge with L298N
  M1 = DC Motor
  M3 = 5-ir-array-sensor [package=THT]
  U1 = SWITCH-SPST-2 [package=switch-spst-vertical]
  VCC1 = Battery block 9V
  hc-sr1 = hc-sr04
  LED1 = LEDs [package=led10mm]
  LED2 = LEDs [package=led10mm]
  LED3 = LEDs [package=led10mm]
  S2 = SWITCH-MOMENTARY-2 [package=tactile-pth-12mm]
  R1 = Resistor [tolerance=±5% resistance=220 package=THT]
  M4 = DC Motor

nets (from the breadboard view):
  N1: MH-ET_LIVE_ESP32_DEVKIT1.IO34, S2.2
  N2: MH-ET_LIVE_ESP32_DEVKIT1.IO35, S1.IN4
  N3: MH-ET_LIVE_ESP32_DEVKIT1.IO32, S1.IN3
  N4: MH-ET_LIVE_ESP32_DEVKIT1.IO33, S1.IN2
  N5: MH-ET_LIVE_ESP32_DEVKIT1.IO27, S1.IN1
  N6: MH-ET_LIVE_ESP32_DEVKIT1.IO12, S1.ENA
  5V: MH-ET_LIVE_ESP32_DEVKIT1.5V, S1.5V, M3.VCC, hc-sr1.VCC, R1.Pin_1
  GND: MH-ET_LIVE_ESP32_DEVKIT1.GND, S1.GND, M3.GND, VCC1.-, hc-sr1.GND, LED1.C, LED2.C, LED3.C
  N7: MH-ET_LIVE_ESP32_DEVKIT1.IO23, hc-sr1.Trig
  N8: MH-ET_LIVE_ESP32_DEVKIT1.IO22, hc-sr1.Echo
  N9: MH-ET_LIVE_ESP32_DEVKIT1.IO19, M3.S5
  N10: MH-ET_LIVE_ESP32_DEVKIT1.IO18, M3.S4
  N11: MH-ET_LIVE_ESP32_DEVKIT1.IO17, M3.S3
  N12: MH-ET_LIVE_ESP32_DEVKIT1.IO16, M3.S2
  N13: MH-ET_LIVE_ESP32_DEVKIT1.IO4, M3.S1
  N14: S1.12V, U1.P
  N15: S1.M1-01, M4.pin_2
  N16: S1.M1-02, M4.pin_1
  N17: S1.M2-01, M1.pin_2
  N18: S1.M2-02, M1.pin_1
  N19: U1.O, VCC1.+

notes:
  LED GROEN
  LED ORANJE
  LED ROOD
  IR sensor
  driver (L298N)
  5V motor
  ultrasone sensor (HC-SR04
  ESP32
  switch
  9V batterij
  drukknop

custom parts:
  MH-ET LIVE ESP32 DEVKIT 38 pins: http://mh.nodebb.com/topic/2/mh-et-live-esp32-devkit
  H-Bridge with L298N: h-bridge
  5-ir-array-sensor: 5 IR array sensor.
